# Fritzing sketch snake (saved by Fritzing 0.9.2b)
breadboards: 2

parts:
  S1 = Pushbutton [package="[THT]"]
  S2 = Pushbutton [package="[THT]"]
  R1 = Resistor [tolerance=±5% resistance=220 package=THT]
  R2 = Resistor [tolerance=±5% resistance=220 package=THT]
  IC1 = SHIFT REGISTER [part_number=SH74HC595 package=dil16]
  IC2 = SHIFT REGISTER [part_number=SH74HC595 package=dil16]
  R3 = Resistor [tolerance=±0.5% resistance=220 package=THT]
  Disp1 = LBT2088AH [part_number=OSL641501-BRA]
  R15 = Resistor [tolerance=±5% resistance=220 package=THT]
  R17 = Resistor [tolerance=±5% resistance=220 package=THT]
  R18 = Resistor [tolerance=±5% resistance=220 package=THT]
  R19 = Resistor [tolerance=±5% resistance=220 package=THT]
  R20 = Resistor [tolerance=±5% resistance=220 package=THT]
  R21 = Resistor [tolerance=±5% resistance=220 package=THT]
  R22 = Resistor [tolerance=±5% resistance=220 package=THT]
  パーツ2 = Arduino Uno (Rev3)

nets:
  N1: S1.Pin_1, S1.Pin_2, R2.Pin_0, パーツ2.D5_PWM
  VCC: S1.Pin_3, S1.Pin_4, S2.Pin_3, S2.Pin_4, IC1.SCL, IC1.VCC, IC2.SCL, IC2.VCC, パーツ2.5V
  N2: S2.Pin_1, S2.Pin_2, R1.Pin_0, パーツ2.D6_PWM
  GND: R1.Pin_1, R2.Pin_1, IC1.GND, IC1.G, IC2.GND, IC2.G, パーツ2.GND
  N3: IC1.QB, R19.Pin_1
  N4: IC1.QC, R17.Pin_0
  N5: IC1.QD, R18.Pin_1
  N6: IC1.QE, R15.Pin_0
  N7: IC1.QF, R20.Pin_0
  N8: IC1.QG, R22.Pin_0
  N9: IC1.QH, R21.Pin_0
  N10: IC1.QH*, IC2.SER
  N11: IC1.SCK, IC2.SCK, パーツ2.D12/MISO
  N12: IC1.RCK, IC2.RCK, パーツ2.D8
  N13: IC1.SER, パーツ2.D11_PWM/MOSI
  N14: IC1.QA, R3.Pin_1
  N15: IC2.QB, Disp1.pin_11
  N16: IC2.QC, Disp1.pin_12
  N17: IC2.QD, Disp1.pin2
  N18: IC2.QE, Disp1.pin_14
  N19: IC2.QF, Disp1.pin_3
  N20: IC2.QG, Disp1.pin_7
  N21: IC2.QH, Disp1.pin_8
  N22: IC2.QA, Disp1.pin_5
  N23: R3.Pin_0, Disp1.pin1
  N24: Disp1.pin_4, R18.Pin_0
  N25: Disp1.pin_6, R19.Pin_0
  N26: Disp1.pin_9, R15.Pin_1
  N27: Disp1.pin_10, R22.Pin_1
  N28: Disp1.pin_13, R21.Pin_1
  N29: Disp1.pin_15, R20.Pin_1
  N30: Disp1.pin_16, R17.Pin_1
